# Fritzing sketch circuit (saved by Fritzing 0.9.3b)
breadboards: 1

parts:
  J1 = STM32 Nucleo boards
  LED2 = smd LED [color="Red (633nm)" package="0603 [SMD]"]
  R1 = Resistor [tolerance=±5% resistance=220 package=THT]

nets:
  N1: J1.D4, R1.Pin_1
  N2: J1.GND, LED2.cathode
  N3: LED2.anode, R1.Pin_0
