# Fritzing sketch circuit (saved by Fritzing 0.9.3b)
breadboards: 1

parts:
  J1 = STM32 Nucleo boards
  R1 = PHOTOCELL [package=photocell]
  R2 = Resistor [tolerance=±5% resistance=1k package=THT]

nets:
  N1: J1.A0, R1.P$2, R2.Pin_0
  N2: J1.5V, R1.P$1
  N3: J1.GND, R2.Pin_1
