# Fritzing sketch circuit (saved by Fritzing 0.9.3b)

parts:
  J1 = STM32 Nucleo boards
  Part1 = Solid State High Level Relay Module [package=relay]
  Lightbulb_socket = Bulb holder (E10) with base
  R1 = 220 Ω Resistor [package=THT]  # not connected

nets:
  N1: J1.D4, Part1.CH1
  N2: J1.5V, Part1.DC+
  N3: J1.GND, Part1.DC-
  N4: Part1.B1, Lightbulb_socket.pin_2

custom parts:
  Solid State High Level Relay Module: 5V Omron solid state relay 240V 2A output with resistance fuse.
  Bulb holder (E10) with base: A bulb holder for an E10 bulb with a base.
  220 Ω Resistor: A generic resistor (0.25W)
