# Fritzing sketch circuit-power (saved by Fritzing 0.9.3b)

parts:
  J1 = STM32 Nucleo boards
  DHT2 = AM2302 DHT22 Humidity and Temperature Sensor
  Part1 = Arduino Uno (Rev3) - ICSP
  Part2 = INA219 High Side DC Current Sensor Breakout [part_number=904]

nets:
  N1: J1.IDD_01, Part2.VIN-
  N2: J1.IDD_02, Part2.VIN+
  N3: J1.D2, DHT2.DAT
  5V: J1.5V, DHT2.VCC
  GND: J1.GND, DHT2.GND
  N4: Part1.A4/SDA, Part2.SCL
  N5: Part1.A5/SCL, Part2.SDA
  5V_2: Part1.5V, Part2.VCC
  GND_2: Part1.GND, Part2.GND

custom parts:
  INA219 High Side DC Current Sensor Breakout: This breakout board will solve all your power-monitoring problems. Instead of struggling with two multimeters, you can just use the handy INA219B chip on this breakout to both measure both the high side voltage and DC current draw over I2C with 1% precision. Most current-measuring devices such as our current panel meter are only good for low side measuring. That means that unless you want to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
