# Fritzing sketch circuit (saved by Fritzing 0.9.3b)

parts:
  J1 = STM32 Nucleo boards
  DHT2 = AM2302 DHT22 Humidity and Temperature Sensor

nets:
  N1: J1.D2, DHT2.DAT
  5V: J1.5V, DHT2.VCC
  GND: J1.GND, DHT2.GND
