# Fritzing sketch circuit (saved by Fritzing 0.9.3b)

parts:
  TFT1 = Color 320x240 TFT Display, ILI9341 Controller Chip
  J1 = STM32 Nucleo boards

nets:
  VCC: TFT1.VCC, J1.3V3
  GND: TFT1.GND, J1.GND
  N1: TFT1.CS, J1.D10_PWM/SS
  N2: TFT1.Reset, J1.D8
  N3: TFT1.D/C, J1.D9_PWM
  N4: TFT1.SDI_(MOSI), J1.D11_PWM/MOSI
  N5: TFT1.SCK, J1.D13/SCK
  N6: TFT1.LED, J1.5V
  N7: TFT1.SDO_(MISO), J1.D12/MISO

custom parts:
  Color 320x240 TFT Display, ILI9341 Controller Chip: 2.2" TFT Display with ILI9341 Controller
